// Logisim project FPA.circ as structural Verilog: 2 circuits, main circuit main
module main (
  input  [31:0] A,
  input  [31:0] B,
  output [31:0] Output,
  output Overflow,
  output Underflow
);

  wire input_1_p3, input_1_p4, input_1_p5, input_1_p6, input_1_p7, main_1_p5, main_1_p6, normalizer_1_p5,
       normalizer_1_p6, rounder_1_p2;
  wire [10:0] rounded_normalizer_1_p2;
  wire [19:0] rounded_normalizer_1_p3_2;
  wire [31:0] rounded_normalizer_1_p3;

  // Input input_1: pin names not known; wires that end beside it: A, B, input_1_p3, input_1_p4, input_1_p5, input_1_p6, input_1_p7
  // adder32bit_main main_1: pin names not known; wires that end beside it: input_1_p5, input_1_p3, input_1_p6, input_1_p7, main_1_p5, main_1_p6
  // normalizer normalizer_1: pin names not known; wires that end beside it: input_1_p4, main_1_p5, Underflow, Overflow, normalizer_1_p5, normalizer_1_p6
  // Rounder rounder_1: pin names not known; wires that end beside it: normalizer_1_p6, rounder_1_p2, rounder_1_p2
  OutputHandler outputhandler_1 (
    .Significand(rounded_normalizer_1_p3_2), .exponent(rounded_normalizer_1_p2), .S(main_1_p6),
    .Output(Output));
  // rounded_normalizer rounded_normalizer_1: pin names not known; wires that end beside it: normalizer_1_p5, rounded_normalizer_1_p2, {rounded_normalizer_1_p3[31:30], rounded_normalizer_1_p3_2, rounded_normalizer_1_p3[9:0]}
endmodule

// OpH
module OutputHandler (
  input  [19:0] Significand,
  input  [10:0] exponent,
  input  S,
  output [31:0] Output
);


  assign Output = {S, exponent, Significand};
endmodule
